# Fritzing sketch Kiln Mains Board (saved by Fritzing 1.0.7)
circuit board: 10.11cm x 5.57719cm

parts:
  J3_SSR_LOAD = Terminal block 2p 7.62mm (41A) [value="41A block" package=THT]
  PS1 = Mean Well IRM-20-12 (20W 12V PCB AC-DC) [value=IRM-20-12 mn="Mean Well" part_number=IRM-20-12 package=THT]
  C1 = Electrolytic Capacitor [value="10µF 35V" capacitance=10µF voltage=35V package="0405 [SMD, electrolytic]"]
  C2 = Electrolytic Capacitor [value="10µF 35V" capacitance=10µF voltage=35V package="0405 [SMD, electrolytic]"]
  LED1_PWR = smd LED [value="green 1206" color=green current=0.030A package="1206 [SMD]"]
  F1 = FUSE [part_number="T1A 5x20mm" value="1A T" package=fuse_5mm]
  MOV1 = Metal oxide varistor 275VAC (14mm disc) [part_number=S14K275 package="THT radial"]
  K2 = TE T92P7D22-12 relay, panel mount (hybrid: no PCB connections) [mn="TE Connectivity" part_number=T92P7D22-12 package="panel mount"]
  A1 = terminal block 3position
  A2 = terminal block 3position
  J4_240V = Terminal block 2p 7.62mm (41A) in [package=THT]
  K3 = TE T92P7D22-12 relay, panel mount (hybrid: no PCB connections) [mn="TE Connectivity" part_number=T92P7D22-12 package="panel mount"]
  J2 = Screw terminal - 2 pins [package=THT]
  J3 = Screw terminal - 2 pins [package=THT]
  D1 = Rectifier Diode [part_number=LL4007 package="Melf DO-213 AB [SMD]"]
  J1 = JST-XH_2.54mm Horizontal SMD Connector 6pin [package=SMD]
  D2 = Rectifier Diode [part_number=LL4007 package="Melf DO-213 AB [SMD]"]
  PS2 = Mean Well IRM-20-12 (20W 12V PCB AC-DC) [value=IRM-20-12 mn="Mean Well" part_number=IRM-20-5 package=THT]
  MH1_body = M2.5 standoff body 5 mm [package="silkscreen only"]  # not connected
  MH2_body = M2.5 standoff body 5 mm [package="silkscreen only"]  # not connected
  MH3_body = M2.5 standoff body 5 mm [package="silkscreen only"]  # not connected
  MH4_body = M2.5 standoff body 5 mm [package="silkscreen only"]  # not connected
  PI_OUTLINE = Raspberry Pi 3B board shadow [package="silkscreen only"]  # not connected
  R3 = Resistor [tolerance=±5% resistance=100 power=0.25W package="1206 [SMD]"]
  R10 = Resistor [tolerance=±5% resistance=10k power=0.25W package="1206 [SMD]"]
  Q2 = MOSFET-NCHANNEL [package=sot23-3]
  C4 = Ceramic Capacitor [capacitance=100nF voltage=35V package="1206 [SMD, multilayer]"]
  C3 = Ceramic Capacitor [capacitance=100nF voltage=35V package="1206 [SMD, multilayer]"]
  Q3 = MOSFET-NCHANNEL [package=sot23-3]
  R11 = Resistor [tolerance=±5% resistance=10k power=0.25W package="1206 [SMD]"]
  R12 = Resistor [tolerance=±5% resistance=100 power=0.25W package="1206 [SMD]"]
  R9 = Resistor [tolerance=±5% resistance=1k power=0.25W package="1206 [SMD]"]

nets:
  N1: J3_SSR_LOAD.1, K2.4
  N2: J3_SSR_LOAD.2, A2.Pin_1, A2.Pin_6
  N3: PS1.AC/L, MOV1.1, K2.6, A1.Pin_5, J4_240V.1, PS2.AC/L
  N4: PS1.AC/N, F1.2, MOV1.2, PS2.AC/N
  12V: PS1.+V, C1.+, K2.A1, K3.A1, J2.pin2, J3.pin2, D1.cathode, J1.pin1, D2.cathode, C3.0
  GND: PS1.-V, C1.-, C2.-, LED1_PWR.cathode, J1.pin6, PS2.-V, R10.Pin_1, Q2.S, C4.1, C3.1, Q3.S, R11.Pin_1
  5V: C2.+, J1.pin2, PS2.+V, C4.0, R9.Pin_0
  N5: LED1_PWR.anode, R9.Pin_1
  N6: F1.1, K2.2, A1.Pin_6, J4_240V.2
  N7: K2.8, A2.Pin_2, A2.Pin_5
  N8: K2.A2, J2.pin1, D1.anode, Q2.D
  N9: K3.A2, J3.pin1, D2.anode, Q3.D
  N10: J1.pin3, R3.Pin_0
  N11: J1.pin4, R12.Pin_0
  N12: R3.Pin_1, R10.Pin_0, Q2.G
  N13: Q3.G, R11.Pin_0, R12.Pin_1

notes:
  J2 → K2 coil — polarity matters
  pin 2 = +12 V
  pin 1 = COIL LOW (Q2 drain)
  D1 cathode is on +12 V. Swap these and D1
  forward-conducts across the rail the moment
  Q2 turns on.
  J3 → K3 coil — polarity matters
  pin 2 = +12 V
  pin 1 = COIL LOW (Q3 drain)
  D2 cathode is on +12 V. Swap these and D2
  forward-conducts across the rail the moment
  Q3 turns on.

custom parts:
  Terminal block 2p 7.62mm (41A): Two-position PCB terminal block on 7.62 mm pitch rated 41 A / 10 mm2 (Phoenix Contact PC 5 series or equivalent). Use for every mains connection on this board - the 5 mm blocks in the Fritzing core top out around 16 A.
  Mean Well IRM-20-12 (20W 12V PCB AC-DC): Mean Well IRM-20-12 encapsulated PCB-mount AC-DC module. 85-264 VAC universal input (non-polarised, so L1-L2 at 240 V is fine), 12 V 1.8 A out, convection cooled, Class II. Footprint from Mean Well case 219A (datasheet bottom view, mirrored here to a top-down footprint).
  Metal oxide varistor 275VAC (14mm disc): 275 VAC-rated metal oxide varistor across the PSU input, 14 mm disc on 7.5 mm lead pitch (TDK S14K275, Littelfuse V275LA20AP or equivalent). Fit it downstream of F1 so a failed MOV blows the fuse rather than the branch circuit breaker.
  TE T92P7D22-12 relay, panel mount (hybrid: no PCB connections): TE / Potter & Brumfield T92 two-pole 30 A relay, 2 form A, 12 VDC coil, panel mount via flanged cover with .250 in (6.35 x 0.81 mm) quick-connect tabs. HYBRID PART: all six terminals are real in schematic and breadboard, so the coil driver and the mains nets connect normally and the sheet documents the real circuit - but every one is hybrid in pcbView, so there is no pad, no ratsnest and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
  Terminal block 2p 7.62mm (41A) in: As TB2_762_kilnmains but drawn with its schematic pins on the right, for terminals that feed the sheet from the left edge.
  JST-XH_2.54mm Horizontal SMD Connector 6pin: JST-XH_2.54mm Horizontal SMD Connector 6pin.
  M2.5 standoff body 5 mm: Silkscreen outline of the 5 mm body of an M2.5 standoff carrying the Raspberry Pi. Keep components and copper clear of it.
  Raspberry Pi 3B board shadow: Silkscreen outline of the Raspberry Pi 3B PCB (85 x 56) as it sits on 35 mm standoffs above this board. Anything needing access from above, the mains input especially, belongs outside it.
